// Logisim project 16-bit  Shift unit.circ as structural Verilog: 1 circuit, main circuit Shift Unit 16-bit
module Shift_Unit_16_bit (
  input  [1:0] Shift_Mode,
  input  [15:0] Shift_input,
  input  [3:0] Shift_Amount,
  output [15:0] Shift_unit_output
);

  wire [15:0] shifter_1_out, shifter_2_out, shifter_3_out;

  Shifter #(.width(16)) shifter_1 (.in(Shift_input), .\dist (Shift_Amount), .out(shifter_1_out));
  Shifter #(.width(16), .shift("lr")) shifter_2 (.in(Shift_input), .\dist (Shift_Amount), .out(shifter_2_out));
  Shifter #(.width(16), .shift("ar")) shifter_3 (.in(Shift_input), .\dist (Shift_Amount), .out(shifter_3_out));
  Multiplexer #(.select(2), .width(16), .enable("false")) multiplexer_1 (
    .in0(Shift_input), .in1(shifter_1_out), .in2(shifter_2_out), .in3(shifter_3_out),
    .out(Shift_unit_output), .sel(Shift_Mode));
endmodule
