// Logisim project 16-bit ADD and SUB.circ as structural Verilog: 1 circuit, main circuit Arithmetic Unit 16-bit
module Arithmetic_Unit_16_bit (
  input  [15:0] A,
  input  [15:0] B,
  input  Select,
  output [15:0] Result,
  output Overflow
);

  wire adder_1_cout, subtractor_1_bout;
  wire [15:0] adder_1_out, subtractor_1_out;

  Adder #(.width(16)) adder_1 (.a(A), .b(B), .out(adder_1_out), .cout(adder_1_cout));  // open: cin
  Subtractor #(.width(16)) subtractor_1 (.a(A), .b(B), .out(subtractor_1_out), .bout(subtractor_1_bout));  // open: bin
  Multiplexer #(.width(16), .enable("false")) multiplexer_1 (
    .in0(adder_1_out), .in1(subtractor_1_out), .out(Result), .sel(Select));
  Multiplexer #(.enable("false")) multiplexer_2 (
    .in0(adder_1_cout), .in1(subtractor_1_bout), .out(Overflow), .sel(Select));
endmodule
