// Logisim project 16-bit Logic unit.circ as structural Verilog: 1 circuit, main circuit Logic Unit 16-bit
module Logic_Unit_16_bit (
  input  [15:0] A,
  input  [15:0] B,
  input  [1:0] Logic_unit_select,
  output [15:0] Logic_unit_output
);

  wire [15:0] and_1_out, not_1_out, or_1_out, xor_1_out;

  assign and_1_out = A & B;  // AND_Gate and_1, 16 bits wide
  assign or_1_out = A | B;  // OR_Gate or_1, 16 bits wide
  assign xor_1_out = A ^ B;  // XOR_Gate xor_1, 16 bits wide
  assign not_1_out = ~or_1_out;  // NOT_Gate not_1, 16 bits wide
  Multiplexer #(.select(2), .width(16), .enable("false")) multiplexer_1 (
    .in0(and_1_out), .in1(or_1_out), .in2(xor_1_out), .in3(not_1_out), .out(Logic_unit_output),
    .sel(Logic_unit_select));

  // Notes on the sheet:
  //   ALU Logic UNIT
endmodule
