// Logisim project 16-bit Pipelined Processor Module.circ as structural Verilog: 1 circuit, main circuit 16-bit Pipelined Processor
module _16_bit_Pipelined_Processor (
  input  Clock,
  output [15:0] Reg_out_0,
  output [15:0] Reg_out_1,
  output [15:0] Reg_out_2,
  output [15:0] Reg_out_3,
  output [15:0] Reg_out_4,
  output [15:0] Reg_out_5,
  output [15:0] Reg_out_6,
  output [15:0] Reg_out_7,
  output [15:0] out_10,
  output [15:0] out_11
);

  wire B_J, BEQZ, BGTZ, BLTZ, button_1_out, button_2_out, button_3_out, button_4_out, button_5_out,
       button_6_out, button_7_out, button_8_out, button_9_out, ExtOp, ExtOpF, Jump_Sel, JumpSelF, MemRd,
       MemRdF, MemRdX, MemWr, MemWrF, pipeline_instruction_mux_1_extopout,
       pipeline_instruction_mux_1_jumpsel, pipeline_instruction_mux_1_memrdin_2,
       pipeline_instruction_mux_1_memwrout, pipeline_instruction_mux_1_regwriteout,
       pipeline_instruction_mux_1_wbselout, pipeline_signal_ex_1_memwrout, pipeline_signal_ex_1_wbselout,
       RegMEM, RegWEX, RegWF, RegWr, stall, WBdata, WBSelF, Zero;
  wire [1:0] Ad__WBSel, Ad_WBSelF, ALUSrc, ALUSrcF, Forward_A, Forward_B, Func, ImmSel, ImmSelF, PCSrc,
       pipeline_instruction_mux_1_ad_wbselout, pipeline_instruction_mux_1_alusecout,
       pipeline_instruction_mux_1_immselout, pipeline_signal_ex_1_ad_wbselout, RegDst;
  wire [2:0] Ra, Rb, Rd, RegW_1, RegW_2, RegW_3, RegW_4;
  wire [3:0] ALUOp, ALUOpF, pipeline_instruction_mux_1_aluopout;
  wire [4:0] Imm5_1, Imm5_2, Op, OpCodeEX, pipeline_instruction_mux_1_opcodeout;
  wire [7:0] Imm8_1, Imm8_2;
  wire [10:0] Imm11_1, Imm11_2;
  wire [15:0] additional_wb_mux_1_to_wbdata, ALU_Out_3, ALU_Out_4, alusrc_mux_1_alu_bin,
       alusrc_mux_2_alu_bin, Branch_Target, Data2Mem, DMOut, forward_mux_a_1_a, forward_mux_b_1_b, Imm16,
       Imm16F, Ins1, instruction_memory_16_bit_1_instruction_out, Jump_Target, NPC_1, NPC_2, PC_2,
       pc_mux_1_pc_input, Ra_1, Ra_2, Rb_1, Rb_2, SSET_out, SSETOutF, to_R7, to_R7F, WB_BUS, WBMux_out;

  PC_Incrementer pc_incrementer_1 (.in_1(out_11), .out_2(out_10));
  PC_Mux pc_mux_1 (
    .Next_PC_Address(out_10), .Jump_Target(Jump_Target), .Branch_Target_Address(Branch_Target),
    .PC_Input(pc_mux_1_pc_input), .PCSrc(PCSrc));
  Button button_1 (.out(button_1_out));
  Program_Counter program_counter_1 (
    .PC_in(pc_mux_1_pc_input), .PC_out(out_11), .Clk(Clock), .PC_Clr(button_1_out), .Disable_PC(stall));
  Hazard_Detect___Forward_and_Stall hazard_detect_forward_and_stall_1 (
    .Rs(Ra), .MemRead(MemRdX), .Rt(Rb), .RegWriteEX(RegWEX), .RegWriteMEM(RegMEM), .Rd2(RegW_2),
    .RegWriteWB(RegWF), .Rd3(RegW_3), .Rd4(RegW_4), .ForwardA(Forward_A), .ForwardB(Forward_B), .Stall(stall));
  Instruction_Memory_16_bit instruction_memory_16_bit_1 (
    .Instruction_Address(out_11), .Instruction_out(instruction_memory_16_bit_1_instruction_out),
    .Disable_IM(stall));
  IM_Pipeline_Register im_pipeline_register_1 (
    .NPC(out_10), .Instruction(instruction_memory_16_bit_1_instruction_out), .NPC_2(NPC_1),
    .Instruction_2(Ins1), .Clock(Clock), .Reset(B_J));
  PC_Control pc_control_1 (
    .Opcode(OpCodeEX), .PCSrc(PCSrc), .BGEZ_flag(BGTZ), .BEQZ_flag(BEQZ), .BLTZ_flag(BLTZ), .B_J(B_J));
  Instruction_Splitter_16_bit instruction_splitter_16_bit_1 (
    .Instruction(Ins1), .Opcodee(Op), .a(Ra), .b(Rb), .d(Rd), .Func(Func), .Imm5(Imm5_1), .Imm8(Imm8_1),
    .Im11(Imm11_1));
  Reg_Mux reg_mux_1 (.Rt(3'b111), .Rw(RegW_1), .Rd(Rd), .RegDst(RegDst), .Ra(Ra));
  Button button_2 (.out(button_2_out));
  Main_Control main_control_1 (
    .Op(Op), .RegDst(RegDst), .RegWr(RegWr), .ExtOp(ExtOp), .ALUSrc(ALUSrc), .MemRd(MemRd), .MemWr(MemWr),
    .WBData(WBdata), .AdditionalWBSel(Ad__WBSel), .out_10(ImmSel), .out_11(Jump_Sel));
  Register_File_8x16_bit register_file_8x16_bit_1 (
    .Write_Data(WB_BUS), .Read_Data_1(Ra_1), .Read_Data_2(Rb_1), .WriteRegister(RegW_4), .RegWrite(RegWF),
    .Clock(Clock), .Read_Register_1(Ra), .Read_Register_2(Rb), .Reg_out_0(Reg_out_0), .Reg_out_1(Reg_out_1),
    .Reg_out_2(Reg_out_2), .Reg_out_3(Reg_out_3), .Reg_out_4(Reg_out_4), .Reg_out_5(Reg_out_5),
    .Reg_out_6(Reg_out_6), .Reg_out_7(Reg_out_7), .clr(button_2_out));
  ALU_Control alu_control_1 (.func(Func), .Op(Op), .ALUOp(ALUOp));
  Forward_Mux_A forward_mux_a_1 (
    .BusA(Ra_1), .ALU_Out(ALU_Out_3), .WBSel_out(WBMux_out), .WB_Reg_our(WB_BUS), .A(forward_mux_a_1_a),
    .ForwwardA(Forward_A));
  Forward_Mux_B forward_mux_b_1 (
    .BusB(Rb_1), .ALU_Out(ALU_Out_3), .WBSel_out(WBMux_out), .WB_Reg_our(WB_BUS), .B(forward_mux_b_1_b),
    .ForwwardB(Forward_B));
  Pipeline_Reg_ID pipeline_reg_id_1 (
    .A(forward_mux_a_1_a), .B(forward_mux_b_1_b), .A_2(Ra_2), .B_2(Rb_2), .Clock(Clock), .NPC2(NPC_1),
    .NPC2_2(NPC_2), .IMM8(Imm8_1), .IMM8_2(Imm8_2), .IMM11(Imm11_1), .IMM11_2(Imm11_2), .IMM5(Imm5_1),
    .IMM5_2(Imm5_2), .RegDst(RegW_1), .RegDst_2(RegW_2), .Clear(button_3_out));
  Button button_3 (.out(button_3_out));
  Pipeline_Instruction_Mux pipeline_instruction_mux_1 (
    .ExtOpIn(ExtOp), .Bubble({5{1'b0}}), .ImmSelIn(ImmSel), .ALUSrcIn(ALUSrc), .JumpSelIn(Jump_Sel),
    .ALUOpIn(ALUOp), .MemRdIn(MemRd), .MemWrIn(MemWr), .WBSelIn(WBdata), .AD_WBSelIN(Ad__WBSel),
    .RegWriteIn(RegWr), .ExtOpOut(pipeline_instruction_mux_1_extopout),
    .ImmSelOut(pipeline_instruction_mux_1_immselout), .ALUSecOut(pipeline_instruction_mux_1_alusecout),
    .JumpSel(pipeline_instruction_mux_1_jumpsel), .ALUOpOut(pipeline_instruction_mux_1_aluopout),
    .MemRdIn_2(pipeline_instruction_mux_1_memrdin_2), .MemWrOut(pipeline_instruction_mux_1_memwrout),
    .WBSelOut(pipeline_instruction_mux_1_wbselout), .AD_WBSelOut(pipeline_instruction_mux_1_ad_wbselout),
    .RegWriteOut(pipeline_instruction_mux_1_regwriteout), .Stall(stall), .OpCodeIn(Op),
    .OpCodeOut(pipeline_instruction_mux_1_opcodeout));
  Jump_Calculator jump_calculator_1 (
    .PC(PC_2), .Jump_Target(Jump_Target), .Imm16(Imm16), .Ra(Ra_2), .Jump_Sel(JumpSelF));
  NPC_to_PC npc_to_pc_1 (.NPC(NPC_2), .PC(PC_2));
  Branch_Caalculator branch_caalculator_1 (
    .Next_PC_Address(NPC_2), ._16_bit_Extended_Immediate(Imm16), .Branch_Target_Address(Branch_Target));
  Pipeline_Signal_EX pipeline_signal_ex_1 (
    .ExtOpIn(pipeline_instruction_mux_1_extopout), .ImmSelIn(pipeline_instruction_mux_1_immselout),
    .ALUSrcIn(pipeline_instruction_mux_1_alusecout), .JumpSelIn(pipeline_instruction_mux_1_jumpsel),
    .ALUOpIn(pipeline_instruction_mux_1_aluopout), .MemRdIn(pipeline_instruction_mux_1_memrdin_2),
    .MemWrIn(pipeline_instruction_mux_1_memwrout), .WBSelIn(pipeline_instruction_mux_1_wbselout),
    .AD_WBSelIN(pipeline_instruction_mux_1_ad_wbselout), .ExtOpOut(ExtOpF), .ImmSelOut(ImmSelF),
    .ALUSecOut(ALUSrcF), .JumpSel(JumpSelF), .ALUOpOut(ALUOpF), .MemRdIn_2(MemRdX),
    .MemWrOut(pipeline_signal_ex_1_memwrout), .WBSelOut(pipeline_signal_ex_1_wbselout),
    .AD_WBSelOut(pipeline_signal_ex_1_ad_wbselout), .Clear(button_4_out), .Clock(Clock),
    .RegWriteIin(pipeline_instruction_mux_1_regwriteout), .RegWriteOut(RegWEX),
    .OpCodeIn(pipeline_instruction_mux_1_opcodeout), .OpCodeOut(OpCodeEX));
  Button button_4 (.out(button_4_out));
  Branch_Flags branch_flags_1 (.A(Ra_2), .A_B(BGTZ), .A___B(BEQZ), .A___B_2(BLTZ));
  Return_Address_unit return_address_unit_1 (.in_1(PC_2), .out_2(to_R7));
  Extender extender_1 (.ImmExt16(Imm16), .ExtOP(ExtOpF), .Imm11(Imm11_2), .ImmSel(ImmSelF));
  SSET_Unit sset_unit_1 (.Imm8(Imm8_2), .SSET_out(SSET_out), .A(Ra_2));
  ALUsrc_Mux alusrc_mux_1 (.Ext(Ra_2), .BusB(Rb_2), .ALU_Bin(alusrc_mux_1_alu_bin), .ALUSrc(ALUSrcF[1]));
  ALUsrc_Mux alusrc_mux_2 (.Ext(Rb_2), .BusB(Imm16), .ALU_Bin(alusrc_mux_2_alu_bin), .ALUSrc(ALUSrcF[0]));
  ALU_16_bit alu_16_bit_1 (
    .A(alusrc_mux_1_alu_bin), .B(alusrc_mux_2_alu_bin), .ALU_Result(ALU_Out_3), .ALU_zero(Zero),
    .ALUOp(ALUOpF));  // open: Overflow
  Pipeline_Reg__MEM pipeline_reg_mem_1 (
    .ALU_output(ALU_Out_3), .Data(Ra_2), .ALU_Output_3(ALU_Out_4), .Data_2(Data2Mem), .RegDst(RegW_2),
    .RegDst_2(RegW_3), .Clock(Clock), .Clear(button_5_out), .Imm16(Imm16), .ALU_Output_2(Imm16F),
    .SSETIn(SSET_out), .SSETOut(SSETOutF), .to_R7(to_R7), .To_R7_2(to_R7F));
  Button button_5 (.out(button_5_out));
  Pipeline_Signal_MEM pipeline_signal_mem_1 (
    .MemRdIn(MemRdX), .MemWrIn(pipeline_signal_ex_1_memwrout), .WBSelIn(pipeline_signal_ex_1_wbselout),
    .AD_WBSelIN(pipeline_signal_ex_1_ad_wbselout), .RegWrite(RegWEX), .MemRdIn_2(MemRdF), .MemWrOut(MemWrF),
    .WBSelOut(WBSelF), .AD_WBSelOut(Ad_WBSelF), .RegWritee(RegMEM), .Clear(button_6_out), .Clock(Clock));
  Button button_6 (.out(button_6_out));
  Button button_7 (.out(button_7_out));
  Data_Memory_16_bit data_memory_16_bit_1 (
    .Address(ALU_Out_4), .Data_in(Data2Mem), .Data_Memory_Output(DMOut), .Store(MemWrF), .Clock(Clock),
    .Load(MemRdF), .Clr(button_7_out));
  Pipeline_Signal_WB pipeline_signal_wb_1 (
    .RegWriteIn(RegMEM), .RegWriteOut(RegWF), .Clock(Clock), .Clear(button_8_out));
  Button button_8 (.out(button_8_out));
  Additional_WB_mux additional_wb_mux_1 (
    .Imm16(Imm16F), .SSETImm16(SSETOutF), .to_WBData(additional_wb_mux_1_to_wbdata), .ALUSrc(WBSelF),
    .ImmSel(Ad_WBSelF), .ALUOut(ALU_Out_4), .to_R7(to_R7F));
  WB_Mux wb_mux_1 (.ALU_out(additional_wb_mux_1_to_wbdata), .Data_Mem_out(DMOut), .Bus_W(WBMux_out), .WB_Data(WBSelF));
  Pipeline_Reg_WB pipeline_reg_wb_1 (
    .RegDst(RegW_3), .RegDst_2(RegW_4), .Clock(Clock), .WBData(WBMux_out), .WBData_2(WB_BUS),
    .Clear(button_9_out));
  Button button_9 (.out(button_9_out));

  // Other names for the same wires on the sheet: ALU_out_f[15:0] = ALU_Out_3; clk = Clock; Next_PC_0[15:0] = out_10;
  //   PC[15:0] = out_11; R0[15:0] = Reg_out_0; R1[15:0] = Reg_out_1; R2[15:0] = Reg_out_2; R3[15:0] = Reg_out_3;
  //   R4[15:0] = Reg_out_4; R5[15:0] = Reg_out_5; R6[15:0] = Reg_out_6; R7[15:0] = Reg_out_7;
  //   WBReg_out[15:0] = WB_BUS

  // Notes on the sheet:
  //   INSTRUCTION FETCH
  //   16-bit Pipelined Processor
  //   ______________________________________________-______________________
  //   Control 
  //   ___________________________________________________________
  //   INSTRUCTION DECODE
  //   Enable
  //   _________
  //   Clock
  //   _________
  //   EXECUTE
  //   Register File Registers R0 - R7
  //   _______________________________________________________
  //   MEMORY ACCESS
  //   WRITE BACK
endmodule
