// Logisim project 16-bit Pippelined Processor Test.circ as structural Verilog: 1 circuit, main circuit main
module main (
  output [15:0] Program_Counter,
  output [15:0] out_2,
  output [15:0] out_3,
  output [15:0] Next_Program_Counter,
  output [15:0] out_5,
  output [15:0] out_6,
  output [15:0] out_7,
  output [15:0] out_8,
  output [15:0] out_9,
  output [15:0] out_10
);

  wire clock_1_out;
  wire [3:0] n16_bit_to_4_bit_1__0, n16_bit_to_4_bit_1__1, n16_bit_to_4_bit_1__2, n16_bit_to_4_bit_1__3,
       n16_bit_to_4_bit_2__0, n16_bit_to_4_bit_2__1, n16_bit_to_4_bit_2__2, n16_bit_to_4_bit_2__3,
       n16_bit_to_4_bit_3__0, n16_bit_to_4_bit_3__1, n16_bit_to_4_bit_3__2, n16_bit_to_4_bit_3__3,
       n16_bit_to_4_bit_4__0, n16_bit_to_4_bit_4__1, n16_bit_to_4_bit_4__2, n16_bit_to_4_bit_4__3,
       n16_bit_to_4_bit_5__0, n16_bit_to_4_bit_5__1, n16_bit_to_4_bit_5__2, n16_bit_to_4_bit_5__3,
       n16_bit_to_4_bit_6__0, n16_bit_to_4_bit_6__1, n16_bit_to_4_bit_6__2, n16_bit_to_4_bit_6__3,
       n16_bit_to_4_bit_7__0, n16_bit_to_4_bit_7__1, n16_bit_to_4_bit_7__2, n16_bit_to_4_bit_7__3,
       n16_bit_to_4_bit_8__0, n16_bit_to_4_bit_8__1, n16_bit_to_4_bit_8__2, n16_bit_to_4_bit_8__3,
       n16_bit_to_4_bit_9__0, n16_bit_to_4_bit_9__1, n16_bit_to_4_bit_9__2, n16_bit_to_4_bit_9__3,
       n16_bit_to_4_bit_10__0, n16_bit_to_4_bit_10__1, n16_bit_to_4_bit_10__2, n16_bit_to_4_bit_10__3;

  Clock clock_1 (.out(clock_1_out));
  Button button_1 ();  // open: out
  Hex_Digit_Display hex_digit_display_1 (.value(n16_bit_to_4_bit_1__3));  // open: dp
  Hex_Digit_Display hex_digit_display_2 (.value(n16_bit_to_4_bit_2__3));  // open: dp
  _16_bit_Pipelined_Processor u_16_bit_pipelined_processor_1 (
    .Reg_out_0(out_2), .Reg_out_4(out_7), .Reg_out_1(out_3), .Reg_out_5(out_8), .Reg_out_2(out_5),
    .Reg_out_6(out_9), .Reg_out_3(out_6), .Reg_out_7(out_10), .Clock(clock_1_out),
    .out_10(Next_Program_Counter), .out_11(Program_Counter));
  Button button_2 ();  // open: out
  Button button_3 ();  // open: out
  Hex_Digit_Display hex_digit_display_3 (.value(n16_bit_to_4_bit_1__2));  // open: dp
  Hex_Digit_Display hex_digit_display_4 (.value(n16_bit_to_4_bit_1__1));  // open: dp
  Hex_Digit_Display hex_digit_display_5 (.value(n16_bit_to_4_bit_2__1));  // open: dp
  Hex_Digit_Display hex_digit_display_6 (.value(n16_bit_to_4_bit_2__2));  // open: dp
  Hex_Digit_Display hex_digit_display_7 (.value(n16_bit_to_4_bit_1__0));  // open: dp
  _16_bit_to_4_bit u_16_bit_to_4_bit_1 (
    .n6_bit_in(Program_Counter), ._0(n16_bit_to_4_bit_1__0), ._1(n16_bit_to_4_bit_1__1),
    ._2(n16_bit_to_4_bit_1__2), ._3(n16_bit_to_4_bit_1__3));
  Hex_Digit_Display hex_digit_display_8 (.value(n16_bit_to_4_bit_2__0));  // open: dp
  _16_bit_to_4_bit u_16_bit_to_4_bit_2 (
    .n6_bit_in(Next_Program_Counter), ._0(n16_bit_to_4_bit_2__0), ._1(n16_bit_to_4_bit_2__1),
    ._2(n16_bit_to_4_bit_2__2), ._3(n16_bit_to_4_bit_2__3));
  Hex_Digit_Display hex_digit_display_9 (.value(n16_bit_to_4_bit_3__2));  // open: dp
  Hex_Digit_Display hex_digit_display_10 (.value(n16_bit_to_4_bit_3__3));  // open: dp
  Hex_Digit_Display hex_digit_display_11 (.value(n16_bit_to_4_bit_4__2));  // open: dp
  Hex_Digit_Display hex_digit_display_12 (.value(n16_bit_to_4_bit_4__3));  // open: dp
  Hex_Digit_Display hex_digit_display_13 (.value(n16_bit_to_4_bit_5__3));  // open: dp
  Hex_Digit_Display hex_digit_display_14 (.value(n16_bit_to_4_bit_5__2));  // open: dp
  Hex_Digit_Display hex_digit_display_15 (.value(n16_bit_to_4_bit_6__2));  // open: dp
  Hex_Digit_Display hex_digit_display_16 (.value(n16_bit_to_4_bit_6__3));  // open: dp
  Hex_Digit_Display hex_digit_display_17 (.value(n16_bit_to_4_bit_7__3));  // open: dp
  Hex_Digit_Display hex_digit_display_18 (.value(n16_bit_to_4_bit_7__2));  // open: dp
  Hex_Digit_Display hex_digit_display_19 (.value(n16_bit_to_4_bit_8__3));  // open: dp
  Hex_Digit_Display hex_digit_display_20 (.value(n16_bit_to_4_bit_8__2));  // open: dp
  Hex_Digit_Display hex_digit_display_21 (.value(n16_bit_to_4_bit_3__1));  // open: dp
  Hex_Digit_Display hex_digit_display_22 (.value(n16_bit_to_4_bit_3__0));  // open: dp
  _16_bit_to_4_bit u_16_bit_to_4_bit_3 (
    .n6_bit_in(out_2), ._0(n16_bit_to_4_bit_3__0), ._1(n16_bit_to_4_bit_3__1), ._2(n16_bit_to_4_bit_3__2),
    ._3(n16_bit_to_4_bit_3__3));
  Hex_Digit_Display hex_digit_display_23 (.value(n16_bit_to_4_bit_4__1));  // open: dp
  Hex_Digit_Display hex_digit_display_24 (.value(n16_bit_to_4_bit_4__0));  // open: dp
  _16_bit_to_4_bit u_16_bit_to_4_bit_4 (
    .n6_bit_in(out_3), ._0(n16_bit_to_4_bit_4__0), ._1(n16_bit_to_4_bit_4__1), ._2(n16_bit_to_4_bit_4__2),
    ._3(n16_bit_to_4_bit_4__3));
  Hex_Digit_Display hex_digit_display_25 (.value(n16_bit_to_4_bit_5__0));  // open: dp
  Hex_Digit_Display hex_digit_display_26 (.value(n16_bit_to_4_bit_5__1));  // open: dp
  _16_bit_to_4_bit u_16_bit_to_4_bit_5 (
    .n6_bit_in(out_5), ._0(n16_bit_to_4_bit_5__0), ._1(n16_bit_to_4_bit_5__1), ._2(n16_bit_to_4_bit_5__2),
    ._3(n16_bit_to_4_bit_5__3));
  Hex_Digit_Display hex_digit_display_27 (.value(n16_bit_to_4_bit_6__1));  // open: dp
  Hex_Digit_Display hex_digit_display_28 (.value(n16_bit_to_4_bit_6__0));  // open: dp
  _16_bit_to_4_bit u_16_bit_to_4_bit_6 (
    .n6_bit_in(out_6), ._0(n16_bit_to_4_bit_6__0), ._1(n16_bit_to_4_bit_6__1), ._2(n16_bit_to_4_bit_6__2),
    ._3(n16_bit_to_4_bit_6__3));
  Hex_Digit_Display hex_digit_display_29 (.value(n16_bit_to_4_bit_7__1));  // open: dp
  Hex_Digit_Display hex_digit_display_30 (.value(n16_bit_to_4_bit_7__0));  // open: dp
  _16_bit_to_4_bit u_16_bit_to_4_bit_7 (
    .n6_bit_in(out_7), ._0(n16_bit_to_4_bit_7__0), ._1(n16_bit_to_4_bit_7__1), ._2(n16_bit_to_4_bit_7__2),
    ._3(n16_bit_to_4_bit_7__3));
  Hex_Digit_Display hex_digit_display_31 (.value(n16_bit_to_4_bit_8__1));  // open: dp
  Hex_Digit_Display hex_digit_display_32 (.value(n16_bit_to_4_bit_8__0));  // open: dp
  _16_bit_to_4_bit u_16_bit_to_4_bit_8 (
    .n6_bit_in(out_8), ._0(n16_bit_to_4_bit_8__0), ._1(n16_bit_to_4_bit_8__1), ._2(n16_bit_to_4_bit_8__2),
    ._3(n16_bit_to_4_bit_8__3));
  Hex_Digit_Display hex_digit_display_33 (.value(n16_bit_to_4_bit_9__2));  // open: dp
  Hex_Digit_Display hex_digit_display_34 (.value(n16_bit_to_4_bit_9__3));  // open: dp
  Hex_Digit_Display hex_digit_display_35 (.value(n16_bit_to_4_bit_10__2));  // open: dp
  Hex_Digit_Display hex_digit_display_36 (.value(n16_bit_to_4_bit_10__3));  // open: dp
  Hex_Digit_Display hex_digit_display_37 (.value(n16_bit_to_4_bit_9__0));  // open: dp
  Hex_Digit_Display hex_digit_display_38 (.value(n16_bit_to_4_bit_9__1));  // open: dp
  _16_bit_to_4_bit u_16_bit_to_4_bit_9 (
    .n6_bit_in(out_9), ._0(n16_bit_to_4_bit_9__0), ._1(n16_bit_to_4_bit_9__1), ._2(n16_bit_to_4_bit_9__2),
    ._3(n16_bit_to_4_bit_9__3));
  Hex_Digit_Display hex_digit_display_39 (.value(n16_bit_to_4_bit_10__0));  // open: dp
  Hex_Digit_Display hex_digit_display_40 (.value(n16_bit_to_4_bit_10__1));  // open: dp
  _16_bit_to_4_bit u_16_bit_to_4_bit_10 (
    .n6_bit_in(out_10), ._0(n16_bit_to_4_bit_10__0), ._1(n16_bit_to_4_bit_10__1),
    ._2(n16_bit_to_4_bit_10__2), ._3(n16_bit_to_4_bit_10__3));

  // Other names for the same wires on the sheet: Next_PC[15:0] = Next_Program_Counter; PC[15:0] = Program_Counter;
  //   R0[15:0] = out_2; R1[15:0] = out_3; R2[15:0] = out_5; R3[15:0] = out_6; R4[15:0] = out_7; R5[15:0] = out_8;
  //   R6[15:0] = out_9; R7[15:0] = out_10

  // Notes on the sheet:
  //   PC
  //   NEXT
  //   PC
  //   16-bit Pipelined Processor Test
  //   Hex
  //   R0
  //   R1
  //   R2
  //   R3
  //   R4
  //   R5
  //   Binary
  //   Registers
  //   R6
  //   R7
endmodule
