// Logisim project 8x16-bit Register File Test.circ as structural Verilog: 1 circuit, main circuit Register File 8x16-bit
module Register_File_8x16_bit (
  input  [2:0] in_1,
  input  [2:0] in_2,
  input  [2:0] in_3,
  input  in_4,
  input  [15:0] in_5,
  output [15:0] Reg_out_0,
  output [15:0] Reg_out_1,
  output [15:0] Reg_out_2,
  output [15:0] Reg_out_3,
  output [15:0] out_10,
  output [15:0] out_11,
  output [15:0] Reg_out_4,
  output [15:0] Reg_out_5,
  output [15:0] Reg_out_6,
  output [15:0] Reg_out_7
);

  wire button_1_out, button_2_out;

  Button button_1 (.out(button_1_out));
  Button button_2 (.out(button_2_out));
  _8x16_bit_Register_File_Register_File_8x16_bit register_file_8x16_bit_1 (
    .Write_Data(in_5), .Read_Data_1(out_10), .Read_Data_2(out_11), .WriteRegister(in_3), .RegWrite(in_4),
    .Clock(button_2_out), .Read_Register_1(in_1), .Read_Register_2(in_2), .Reg_out_0(Reg_out_0),
    .Reg_out_1(Reg_out_1), .Reg_out_2(Reg_out_2), .Reg_out_3(Reg_out_3), .Reg_out_4(Reg_out_4),
    .Reg_out_5(Reg_out_5), .Reg_out_6(Reg_out_6), .Reg_out_7(Reg_out_7), .clr(button_1_out));

  // Notes on the sheet:
  //   8x16-bit Register File Test
  //   Test Result: OK
endmodule
