// Logisim project ALU Control.circ as structural Verilog: 1 circuit, main circuit ALU Control
module ALU_Control (
  input  [1:0] func,
  input  [4:0] Op,
  output [3:0] ALUOp
);

  wire _0, _1, _2, _3, _4, _5, _6, _7, _8, _9, _10, _11, _12, _13, _14, _15, _16, _17, _18, _19, _20, _21,
       _22, _23, _24, _25, _26, _27, _28, _29, _30, _31, ADD, AND, and_1_out, and_2_out, and_3_out,
       and_4_out, and_5_out, and_6_out, and_7_out, and_8_out, LOGIC, NOR, not_1_out, not_2_out, not_3_out,
       not_4_out, not_5_out, not_6_out, not_7_out, not_8_out, OR, SEQ, SLT, SUB, XOR;

  not not_1 (not_1_out, func[1]);
  not not_2 (not_2_out, func[0]);
  and and_1 (and_1_out, _1, not_2_out, not_1_out);
  Decoder #(.select(5)) decoder_1 (
    .out0(_0), .out1(_1), .out2(_2), .out3(_3), .out4(_4), .out5(_5), .out6(_6), .out7(_7), .out8(_8),
    .out9(_9), .out10(_10), .out11(_11), .out12(_12), .out13(_13), .out14(_14), .out15(_15), .out16(_16),
    .out17(_17), .out18(_18), .out19(_19), .out20(_20), .out21(_21), .out22(_22), .out23(_23), .out24(_24),
    .out25(_25), .out26(_26), .out27(_27), .out28(_28), .out29(_29), .out30(_30), .out31(_31), .sel(Op),
    .en(1'b1));
  or or_1 (ADD, and_1_out, _16, _17, _30, _8);
  or or_2 (ALUOp[3], ADD, SUB, LOGIC);
  not not_3 (not_3_out, func[1]);
  and and_2 (and_2_out, _1, func[0], not_3_out);
  or or_3 (SUB, and_2_out, _9);
  or or_4 (ALUOp[2], LOGIC, SLT, SEQ);
  not not_4 (not_4_out, func[0]);
  and and_3 (and_3_out, _1, not_4_out, func[1]);
  or or_5 (SLT, and_3_out, _10);
  and and_4 (and_4_out, _1, func[0], func[1]);
  or or_6 (SEQ, and_4_out, _11);
  or or_7 (ALUOp[1], _13, XOR, NOR);
  not not_5 (not_5_out, func[0]);
  not not_6 (not_6_out, func[1]);
  and and_5 (and_5_out, _0, not_5_out, not_6_out);
  or or_8 (AND, and_5_out, _4);
  or or_9 (ALUOp[0], OR, NOR, SUB, SLT, _12);
  not not_7 (not_7_out, func[1]);
  and and_6 (and_6_out, _0, func[0], not_7_out);
  or or_10 (OR, and_6_out, _5);
  not not_8 (not_8_out, func[0]);
  and and_7 (and_7_out, _0, not_8_out, func[1]);
  or or_11 (XOR, and_7_out, _6);
  or or_12 (LOGIC, AND, OR, XOR, NOR);
  and and_8 (and_8_out, _0, func[0], func[1]);
  or or_13 (NOR, and_8_out, _7);

  // Other names for the same wires on the sheet: F0 = func[0]; F1 = func[1]; SLL = _12; SRL = _13

  // Notes on the sheet:
  //   Inputs: Opcode 5-bit          func 2-bit
  //   ALU Control 
  //   Output: ALUOp 4-bit
endmodule
