// Logisim project Additional WB Mux.circ as structural Verilog: 1 circuit, main circuit Additional WB mux
module Additional_WB_mux (
  input  [15:0] ALUOut,
  input  [15:0] Imm16,
  input  [15:0] SSETImm16,
  input  [15:0] to_R7,
  input  [1:0] ImmSel,
  input  ALUSrc,
  output [15:0] to_WBData
);

  wire [0:0] or_1_out;

  Multiplexer #(.select(2), .width(16), .enable("false")) multiplexer_1 (
    .in0(ALUOut), .in1(Imm16), .in2(SSETImm16), .in3(to_R7), .out(to_WBData), .sel({ImmSel[1], or_1_out[0]}));
  or or_1 (or_1_out[0], ImmSel[0], ALUSrc);
endmodule
