// Logisim project Branch Comparator.circ as structural Verilog: 1 circuit, main circuit Branch Flags
module Branch_Flags (
  input  [15:0] A,
  output A_B,
  output A___B,
  output A___B_2
);

  Comparator #(.width(16)) comparator_1 (.a(A), .b({16{1'b0}}), .gt(A_B), .eq(A___B), .lt(A___B_2));
endmodule
