// Logisim project Data Memory.circ as structural Verilog: 1 circuit, main circuit Data Memory 16-bit
module Data_Memory_16_bit (
  input  [15:0] Address,
  input  [15:0] Data_in,
  input  Store,
  input  Clock,
  input  Load,
  input  Clr,
  output [15:0] Data_Memory_Output
);

  RAM #(.addrWidth(16), .dataWidth(16), .bus("separate")) ram_1 (
    .addr(Address), .din(Data_in), .data(Data_Memory_Output), .str(Store), .sel(1'b1), .clk(Clock),
    .ld(Load), .clr(Clr));
endmodule
