// Logisim project Extender.circ as structural Verilog: 1 circuit, main circuit Extender
module Extender (
  input  [1:0] ImmSel,
  input  [10:0] Imm11,
  input  ExtOP,
  output [15:0] ImmExt16
);

  wire [15:0] bit_extender_1_out, bit_extender_2_out, bit_extender_3_out, bit_extender_4_out,
       bit_extender_5_out, bit_extender_6_out, multiplexer_1_out, multiplexer_2_out, multiplexer_3_out;

  assign bit_extender_1_out = {{11{1'b0}}, Imm11[4:0]};  // Bit_Extender bit_extender_1
  assign bit_extender_2_out = {{11{Imm11[4]}}, Imm11[4:0]};  // Bit_Extender bit_extender_2
  assign bit_extender_3_out = {{8{1'b0}}, Imm11[7:0]};  // Bit_Extender bit_extender_3
  assign bit_extender_4_out = {{8{Imm11[7]}}, Imm11[7:0]};  // Bit_Extender bit_extender_4
  assign bit_extender_5_out = {{5{1'b0}}, Imm11};  // Bit_Extender bit_extender_5
  assign bit_extender_6_out = {{5{Imm11[10]}}, Imm11};  // Bit_Extender bit_extender_6
  Multiplexer #(.width(16)) multiplexer_1 (
    .in0(bit_extender_1_out), .in1(bit_extender_2_out), .out(multiplexer_1_out), .sel(ExtOP), .en(1'b1));
  Multiplexer #(.width(16)) multiplexer_2 (
    .in0(bit_extender_3_out), .in1(bit_extender_4_out), .out(multiplexer_2_out), .sel(ExtOP), .en(1'b1));
  Multiplexer #(.width(16)) multiplexer_3 (
    .in0(bit_extender_5_out), .in1(bit_extender_6_out), .out(multiplexer_3_out), .sel(ExtOP), .en(1'b1));
  Multiplexer #(.select(2), .width(16), .enable("false")) multiplexer_4 (
    .in0(multiplexer_1_out), .in1(multiplexer_2_out), .in2(multiplexer_3_out), .out(ImmExt16), .sel(ImmSel));  // open: in3

  // Notes on the sheet:
  //   J-Type Imm5
  //   B-Type Imm8
  //   Extend to 16 bit from :
endmodule
