// Logisim project Forward ,Hazard and Stall Unit.circ as structural Verilog: 1 circuit, main circuit Hazard Detect , Forward and Stall
module Hazard_Detect___Forward_and_Stall (
  input  [2:0] Rs,
  input  MemRead,
  input  [2:0] Rt,
  input  RegWriteEX,
  input  RegWriteMEM,
  input  [2:0] Rd2,
  input  RegWriteWB,
  input  [2:0] Rd3,
  input  [2:0] Rd4,
  output [1:0] ForwardA,
  output [1:0] ForwardB,
  output Stall
);

  wire FwdA_1, FwdA_2, FwdA_3, FwdB_1, FwdB_2, FwdB_3, or_5_out, Rs_Rd2, Rs_Rd3, Rs_Rd4, Rt_Rd2, Rt_Rd3,
       Rt_Rd4;

  and and_1 (FwdA_1, Rs_Rd2, RegWriteEX);
  or or_1 (ForwardA[1], FwdA_2, FwdA_3);
  and and_2 (FwdA_2, Rs_Rd3, RegWriteMEM);
  or or_2 (ForwardA[0], FwdA_1, FwdA_3);
  and and_3 (FwdA_3, Rs_Rd4, RegWriteWB);
  Comparator #(.width(3), .mode("unsigned")) comparator_1 (.a(Rs), .b(Rd2), .eq(Rs_Rd2));  // open: gt, lt
  Comparator #(.width(3), .mode("unsigned")) comparator_2 (.a(Rs), .b(Rd3), .eq(Rs_Rd3));  // open: gt, lt
  Comparator #(.width(3), .mode("unsigned")) comparator_3 (.a(Rs), .b(Rd4), .eq(Rs_Rd4));  // open: gt, lt
  and and_4 (FwdB_1, Rt_Rd2, RegWriteEX);
  or or_3 (ForwardB[1], FwdB_2, FwdB_3);
  Comparator #(.width(3), .mode("unsigned")) comparator_4 (.a(Rt), .b(Rd2), .eq(Rt_Rd2));  // open: gt, lt
  Comparator #(.width(3), .mode("unsigned")) comparator_5 (.a(Rt), .b(Rd3), .eq(Rt_Rd3));  // open: gt, lt
  Comparator #(.width(3), .mode("unsigned")) comparator_6 (.a(Rt), .b(Rd4), .eq(Rt_Rd4));  // open: gt, lt
  and and_5 (FwdB_2, Rt_Rd3, RegWriteMEM);
  or or_4 (ForwardB[0], FwdB_1, FwdB_3);
  and and_6 (FwdB_3, Rt_Rd4, RegWriteWB);
  and and_7 (Stall, MemRead, or_5_out);
  or or_5 (or_5_out, FwdA_1, FwdB_1);
endmodule
