// Logisim project Forward Mux A.circ as structural Verilog: 1 circuit, main circuit Forward Mux A
module Forward_Mux_A (
  input  [15:0] BusA,
  input  [15:0] ALU_Out,
  input  [15:0] WBSel_out,
  input  [1:0] ForwwardA,
  input  [15:0] WB_Reg_our,
  output [15:0] A
);

  Multiplexer #(.select(2), .width(16), .enable("false")) multiplexer_1 (
    .in0(BusA), .in1(ALU_Out), .in2(WBSel_out), .in3(WB_Reg_our), .out(A), .sel(ForwwardA));
endmodule
