// Logisim project Forward Mux B.circ as structural Verilog: 1 circuit, main circuit Forward Mux B
module Forward_Mux_B (
  input  [15:0] BusB,
  input  [15:0] ALU_Out,
  input  [15:0] WBSel_out,
  input  [1:0] ForwwardB,
  input  [15:0] WB_Reg_our,
  output [15:0] B
);

  Multiplexer #(.select(2), .width(16), .enable("false")) multiplexer_1 (
    .in0(BusB), .in1(ALU_Out), .in2(WBSel_out), .in3(WB_Reg_our), .out(B), .sel(ForwwardB));
endmodule
