// Logisim project Instruction Memory.circ as structural Verilog: 1 circuit, main circuit Instruction Memory 16-bit
module Instruction_Memory_16_bit (
  input  [15:0] Instruction_Address,
  input  Disable_IM,
  output [15:0] Instruction_out
);

  wire not_1_out;

  not not_1 (not_1_out, Disable_IM);
  ROM #(.addrWidth(16), .dataWidth(16)) rom_1 (.addr(Instruction_Address), .data(Instruction_out), .sel(not_1_out));
endmodule
