// Logisim project NPC2PC.circ as structural Verilog: 1 circuit, main circuit NPC to PC
module NPC_to_PC (
  input  [15:0] NPC,
  output [15:0] PC
);

  Subtractor #(.width(16)) subtractor_1 (.a(NPC), .b(16'h2), .out(PC));  // open: bin, bout
endmodule
