// Logisim project PC Control Test.circ as structural Verilog: 1 circuit, main circuit main
module main (
  input  in_1,
  input  [4:0] in_2,
  input  in_3,
  input  in_4,
  output [1:0] out_5
);

  PC_Control pc_control_1 (.Opcode(in_2), .PCSrc(out_5), .BGEZ_flag(in_1), .BEQZ_flag(in_3), .BLTZ_flag(in_4));
endmodule
