// Logisim project PC Control.circ as structural Verilog: 1 circuit, main circuit PC Control
module PC_Control (
  input  [4:0] Opcode,
  input  BGEZ_flag,
  input  BEQZ_flag,
  input  BLTZ_flag,
  output [1:0] PCSrc,
  output B_J
);

  wire _0, _1, _2, _3, _4, _5, _6, _7, _8, _9, _10, _11, _12, _13, _14, _15, _16, _17, _18, _19, _20, _21,
       _22, _23, _24, _25, _26, _27, _28, _29, _30, _31, and_1_out, and_2_out, and_3_out, and_4_out,
       and_5_out, and_6_out, and_7_out, and_8_out, Inc, not_1_out, not_2_out, not_3_out, not_4_out,
       not_5_out, not_6_out, not_7_out, not_8_out, not_9_out, not_10_out, not_11_out, not_12_out, not_13_out,
       not_14_out, not_15_out, not_16_out, or_2_out, or_5_out, or_6_out;

  Decoder #(.select(5)) decoder_1 (
    .out0(_0), .out1(_1), .out2(_2), .out3(_3), .out4(_4), .out5(_5), .out6(_6), .out7(_7), .out8(_8),
    .out9(_9), .out10(_10), .out11(_11), .out12(_12), .out13(_13), .out14(_14), .out15(_15), .out16(_16),
    .out17(_17), .out18(_18), .out19(_19), .out20(_20), .out21(_21), .out22(_22), .out23(_23), .out24(_24),
    .out25(_25), .out26(_26), .out27(_27), .out28(_28), .out29(_29), .out30(_30), .out31(_31), .sel(Opcode),
    .en(1'b1));
  or or_1 (B_J, PCSrc[0], PCSrc[1]);
  or or_2 (or_2_out, _0, _1, _4, _5, _6, _7, _8, _9, _10, _12, _13, _14, _15, _16, _17, _28, _29, _11);
  or or_3 (Inc, or_2_out, not_1_out);
  not not_1 (not_1_out, PCSrc[0]);
  or or_4 (PCSrc[1], _26, _27, _30, _31);
  not not_2 (not_2_out, BLTZ_flag);
  not not_3 (not_3_out, BGEZ_flag);
  and and_1 (and_1_out, _20, not_3_out, BEQZ_flag, not_2_out);
  not not_4 (not_4_out, BEQZ_flag);
  not not_5 (not_5_out, BGEZ_flag);
  and and_2 (and_2_out, _21, not_5_out, not_4_out, BLTZ_flag);
  not not_6 (not_6_out, BEQZ_flag);
  not not_7 (not_7_out, BLTZ_flag);
  and and_3 (and_3_out, _21, BGEZ_flag, not_6_out, not_7_out);
  or or_5 (or_5_out, and_2_out, and_3_out);
  not not_8 (not_8_out, BGEZ_flag);
  not not_9 (not_9_out, BEQZ_flag);
  and and_4 (and_4_out, _22, not_8_out, not_9_out, BLTZ_flag);
  not not_10 (not_10_out, BLTZ_flag);
  not not_11 (not_11_out, BGEZ_flag);
  and and_5 (and_5_out, _23, not_11_out, BEQZ_flag, not_10_out);
  or or_6 (or_6_out, and_5_out, and_6_out);
  or or_7 (PCSrc[0], and_1_out, or_5_out, and_4_out, or_6_out, and_7_out, and_8_out);
  not not_12 (not_12_out, BLTZ_flag);
  not not_13 (not_13_out, BEQZ_flag);
  and and_6 (and_6_out, _23, BGEZ_flag, not_13_out, not_12_out);
  not not_14 (not_14_out, BLTZ_flag);
  not not_15 (not_15_out, BEQZ_flag);
  and and_7 (and_7_out, _24, BGEZ_flag, not_15_out, not_14_out);
  and and_8 (and_8_out, _25, not_16_out);
  not not_16 (not_16_out, BGEZ_flag);

  // Other names for the same wires on the sheet: BEQZ = BEQZ_flag; BGEZ = BGEZ_flag; BLTZ = BLTZ_flag; B = PCSrc[0];
  //   PCScr[1:0] = PCSrc; J = PCSrc[1]

  // Notes on the sheet:
  //   Inputs: Opcode 5-bit        ZERO,BGEZ,BEQZ,BLEZ Flags
  //   PC Control
  //   _____________________
  //   Output: PCScr 2-bit
endmodule
