// Logisim project Pipeline Instruction Stall Mux.circ as structural Verilog: 1 circuit, main circuit Pipeline Instruction Mux
module Pipeline_Instruction_Mux (
  input  ExtOpIn,
  input  [4:0] Bubble,
  input  [1:0] ImmSelIn,
  input  [1:0] ALUSrcIn,
  input  JumpSelIn,
  input  [3:0] ALUOpIn,
  input  MemRdIn,
  input  MemWrIn,
  input  WBSelIn,
  input  [1:0] AD_WBSelIN,
  input  RegWriteIn,
  input  [4:0] OpCodeIn,
  input  Stall,
  output ExtOpOut,
  output [1:0] ImmSelOut,
  output [1:0] ALUSecOut,
  output JumpSel,
  output [3:0] ALUOpOut,
  output MemRdIn_2,
  output MemWrOut,
  output WBSelOut,
  output [1:0] AD_WBSelOut,
  output RegWriteOut,
  output [4:0] OpCodeOut
);

  Multiplexer #(.enable("false")) multiplexer_1 (.in0(ExtOpIn), .in1(Bubble[0]), .out(ExtOpOut), .sel(Stall));
  Multiplexer #(.width(2), .enable("false")) multiplexer_2 (
    .in0(ImmSelIn), .in1(Bubble[2:1]), .out(ImmSelOut), .sel(Stall));
  Multiplexer #(.width(2), .enable("false")) multiplexer_3 (
    .in0(ALUSrcIn), .in1(Bubble[2:1]), .out(ALUSecOut), .sel(Stall));
  Multiplexer #(.enable("false")) multiplexer_4 (.in0(JumpSelIn), .in1(Bubble[0]), .out(JumpSel), .sel(Stall));
  Multiplexer #(.width(4), .enable("false")) multiplexer_5 (
    .in0(ALUOpIn), .in1(Bubble[3:0]), .out(ALUOpOut), .sel(Stall));
  Multiplexer #(.enable("false")) multiplexer_6 (.in0(MemRdIn), .in1(Bubble[0]), .out(MemRdIn_2), .sel(Stall));
  Multiplexer #(.enable("false")) multiplexer_7 (.in0(MemWrIn), .in1(Bubble[0]), .out(MemWrOut), .sel(Stall));
  Multiplexer #(.enable("false")) multiplexer_8 (.in0(WBSelIn), .in1(Bubble[0]), .out(WBSelOut), .sel(Stall));
  Multiplexer #(.width(2), .enable("false")) multiplexer_9 (
    .in0(AD_WBSelIN), .in1(Bubble[2:1]), .out(AD_WBSelOut), .sel(Stall));
  Multiplexer #(.enable("false")) multiplexer_10 (.in0(RegWriteIn), .in1(Bubble[0]), .out(RegWriteOut), .sel(Stall));
  Multiplexer #(.width(5), .enable("false")) multiplexer_11 (
    .in0(OpCodeIn), .in1(Bubble), .out(OpCodeOut), .sel(Stall));
endmodule
