// Logisim project Pipeline Reg ID.circ as structural Verilog: 1 circuit, main circuit Pipeline Reg ID
module Pipeline_Reg_ID (
  input  [4:0] IMM5,
  input  [7:0] IMM8,
  input  [10:0] IMM11,
  input  [15:0] NPC2,
  input  [15:0] A,
  input  [15:0] B,
  input  [2:0] RegDst,
  input  Clock,
  input  Clear,
  output [4:0] IMM5_2,
  output [7:0] IMM8_2,
  output [10:0] IMM11_2,
  output [15:0] NPC2_2,
  output [15:0] A_2,
  output [15:0] B_2,
  output [2:0] RegDst_2
);

  Register #(.width(5)) IMM16 (.D(IMM5), .en(1'b1), .Q(IMM5_2), .clk(Clock), .clr(Clear));
  Register u_IMM8 (.D(IMM8), .en(1'b1), .Q(IMM8_2), .clk(Clock), .clr(Clear));
  Register #(.width(11)) u_IMM11 (.D(IMM11), .en(1'b1), .Q(IMM11_2), .clk(Clock), .clr(Clear));
  Register #(.width(16)) u_NPC2 (.D(NPC2), .en(1'b1), .Q(NPC2_2), .clk(Clock), .clr(Clear));
  Register #(.width(16)) u_A (.D(A), .en(1'b1), .Q(A_2), .clk(Clock), .clr(Clear));
  Register #(.width(16)) u_B (.D(B), .en(1'b1), .Q(B_2), .clk(Clock), .clr(Clear));
  Register #(.width(3)) u_RegDst (.D(RegDst), .en(1'b1), .Q(RegDst_2), .clk(Clock), .clr(Clear));
endmodule
