// Logisim project Pipeline Reg IF.circ as structural Verilog: 1 circuit, main circuit IM Pipeline Register
module IM_Pipeline_Register (
  input  [15:0] NPC,
  input  [15:0] Instruction,
  input  Clock,
  input  Reset,
  output [15:0] NPC_2,
  output [15:0] Instruction_2
);

  Register #(.width(16)) u_NPC (.D(NPC), .en(1'b1), .Q(NPC_2), .clk(Clock), .clr(Reset));
  Register #(.width(16)) u_Instruction (.D(Instruction), .en(1'b1), .Q(Instruction_2), .clk(Clock), .clr(Reset));
endmodule
