// Logisim project Pipeline Reg MEM.circ as structural Verilog: 1 circuit, main circuit Pipeline Reg  MEM
module Pipeline_Reg__MEM (
  input  [15:0] to_R7,
  input  [15:0] SSETIn,
  input  [15:0] Imm16,
  input  [15:0] ALU_output,
  input  [15:0] Data,
  input  [2:0] RegDst,
  input  Clock,
  input  Clear,
  output [15:0] To_R7_2,
  output [15:0] SSETOut,
  output [15:0] ALU_Output_2,
  output [15:0] ALU_Output_3,
  output [15:0] Data_2,
  output [2:0] RegDst_2
);

  Register #(.width(16)) u_to_R7 (.D(to_R7), .en(1'b1), .Q(To_R7_2), .clk(Clock), .clr(Clear));
  Register #(.width(16)) SSET (.D(SSETIn), .en(1'b1), .Q(SSETOut), .clk(Clock), .clr(Clear));
  Register #(.width(16)) u_Imm16 (.D(Imm16), .en(1'b1), .Q(ALU_Output_2), .clk(Clock), .clr(Clear));
  Register #(.width(16)) u_ALU_Output (.D(ALU_output), .en(1'b1), .Q(ALU_Output_3), .clk(Clock), .clr(Clear));
  Register #(.width(16)) u_Data (.D(Data), .en(1'b1), .Q(Data_2), .clk(Clock), .clr(Clear));
  Register #(.width(3)) u_RegDst (.D(RegDst), .en(1'b1), .Q(RegDst_2), .clk(Clock), .clr(Clear));
endmodule
