// Logisim project Pipeline Reg WB.circ as structural Verilog: 1 circuit, main circuit Pipeline Reg WB
module Pipeline_Reg_WB (
  input  [15:0] WBData,
  input  [2:0] RegDst,
  input  Clock,
  input  Clear,
  output [15:0] WBData_2,
  output [2:0] RegDst_2
);

  Register #(.width(16)) u_WBData (.D(WBData), .en(1'b1), .Q(WBData_2), .clk(Clock), .clr(Clear));
  Register #(.width(3)) u_RegDst (.D(RegDst), .en(1'b1), .Q(RegDst_2), .clk(Clock), .clr(Clear));
endmodule
