// Logisim project Pipeline Signal EX.circ as structural Verilog: 1 circuit, main circuit Pipeline Signal EX
module Pipeline_Signal_EX (
  input  ExtOpIn,
  input  [1:0] ImmSelIn,
  input  [1:0] ALUSrcIn,
  input  JumpSelIn,
  input  [3:0] ALUOpIn,
  input  MemRdIn,
  input  MemWrIn,
  input  WBSelIn,
  input  [1:0] AD_WBSelIN,
  input  RegWriteIin,
  input  [4:0] OpCodeIn,
  input  Clear,
  input  Clock,
  output ExtOpOut,
  output [1:0] ImmSelOut,
  output [1:0] ALUSecOut,
  output JumpSel,
  output [3:0] ALUOpOut,
  output MemRdIn_2,
  output MemWrOut,
  output WBSelOut,
  output [1:0] AD_WBSelOut,
  output RegWriteOut,
  output [4:0] OpCodeOut
);

  Register #(.width(1)) ExtOp (.D(ExtOpIn), .en(1'b1), .Q(ExtOpOut), .clk(Clock), .clr(Clear));
  Register #(.width(2)) ImmSel (.D(ImmSelIn), .en(1'b1), .Q(ImmSelOut), .clk(Clock), .clr(Clear));
  Register #(.width(2)) ALUSrc (.D(ALUSrcIn), .en(1'b1), .Q(ALUSecOut), .clk(Clock), .clr(Clear));
  Register #(.width(1)) u_JumpSel (.D(JumpSelIn), .en(1'b1), .Q(JumpSel), .clk(Clock), .clr(Clear));
  Register #(.width(4)) ALUOp (.D(ALUOpIn), .en(1'b1), .Q(ALUOpOut), .clk(Clock), .clr(Clear));
  Register #(.width(1)) MemRd (.D(MemRdIn), .en(1'b1), .Q(MemRdIn_2), .clk(Clock), .clr(Clear));
  Register #(.width(1)) MemWr (.D(MemWrIn), .en(1'b1), .Q(MemWrOut), .clk(Clock), .clr(Clear));
  Register #(.width(1)) WBSel (.D(WBSelIn), .en(1'b1), .Q(WBSelOut), .clk(Clock), .clr(Clear));
  Register #(.width(2)) AD_WBSel (.D(AD_WBSelIN), .en(1'b1), .Q(AD_WBSelOut), .clk(Clock), .clr(Clear));
  Register #(.width(1)) RegWrite (.D(RegWriteIin), .en(1'b1), .Q(RegWriteOut), .clk(Clock), .clr(Clear));
  Register #(.width(5)) OpCode (.D(OpCodeIn), .en(1'b1), .Q(OpCodeOut), .clk(Clock), .clr(Clear));
endmodule
