// Logisim project Pipeline Signal MEM.circ as structural Verilog: 1 circuit, main circuit Pipeline Signal MEM
module Pipeline_Signal_MEM (
  input  MemRdIn,
  input  MemWrIn,
  input  WBSelIn,
  input  [1:0] AD_WBSelIN,
  input  RegWrite,
  input  Clear,
  input  Clock,
  output MemRdIn_2,
  output MemWrOut,
  output WBSelOut,
  output [1:0] AD_WBSelOut,
  output RegWritee
);

  Register #(.width(1)) MemRd (.D(MemRdIn), .en(1'b1), .Q(MemRdIn_2), .clk(Clock), .clr(Clear));
  Register #(.width(1)) MemWr (.D(MemWrIn), .en(1'b1), .Q(MemWrOut), .clk(Clock), .clr(Clear));
  Register #(.width(1)) WBSel (.D(WBSelIn), .en(1'b1), .Q(WBSelOut), .clk(Clock), .clr(Clear));
  Register #(.width(2)) AD_WBSel (.D(AD_WBSelIN), .en(1'b1), .Q(AD_WBSelOut), .clk(Clock), .clr(Clear));
  Register #(.width(1)) u_RegWrite (.D(RegWrite), .en(1'b1), .Q(RegWritee), .clk(Clock), .clr(Clear));
endmodule
