// Logisim project Pipeline Signal WB.circ as structural Verilog: 1 circuit, main circuit Pipeline Signal WB
module Pipeline_Signal_WB (
  input  RegWriteIn,
  input  Clock,
  input  Clear,
  output RegWriteOut
);

  Register #(.width(1)) register_1 (.D(RegWriteIn), .en(1'b1), .Q(RegWriteOut), .clk(Clock), .clr(Clear));
endmodule
