// Logisim project Program Counter 16-bit.circ as structural Verilog: 1 circuit, main circuit Program Counter
module Program_Counter (
  input  [15:0] PC_in,
  input  Clk,
  input  PC_Clr,
  input  Disable_PC,
  output [15:0] PC_out
);

  wire not_1_out;

  Register #(.width(16)) register_1 (.D(PC_in), .en(not_1_out), .Q(PC_out), .clk(Clk), .clr(PC_Clr));
  not not_1 (not_1_out, Disable_PC);
endmodule
