// Logisim project Register Destination Mux.circ as structural Verilog: 1 circuit, main circuit Reg Mux
module Reg_Mux (
  input  [2:0] Rt,
  input  [2:0] Rd,
  input  [2:0] Ra,
  input  [1:0] RegDst,
  output [2:0] Rw
);

  Multiplexer #(.select(2), .width(3), .enable("false")) multiplexer_1 (
    .in0(Rt), .in1(Rd), .in2(Ra), .out(Rw), .sel(RegDst));  // open: in3
endmodule
