// Logisim project SSET Unit.circ as structural Verilog: 1 circuit, main circuit SSET Unit
module SSET_Unit (
  input  [15:0] A,
  input  [7:0] Imm8,
  output [15:0] SSET_out
);


  assign SSET_out = {A[7:0], Imm8};
endmodule
