// Logisim project Write Back Mux.circ as structural Verilog: 1 circuit, main circuit WB Mux
module WB_Mux (
  input  [15:0] ALU_out,
  input  [15:0] Data_Mem_out,
  input  WB_Data,
  output [15:0] Bus_W
);

  Multiplexer #(.width(16)) multiplexer_1 (.in0(ALU_out), .in1(Data_Mem_out), .out(Bus_W), .sel(WB_Data), .en(1'b1));
endmodule
