// Logisim project 16-bit ALU Revised.circ as structural Verilog: 1 circuit, main circuit ALU 16-bit
module ALU_16_bit (
  input  [15:0] A,
  input  [15:0] B,
  input  [3:0] ALUOp,
  output Overflow,
  output [15:0] ALU_Result,
  output ALU_zero
);

  wire [15:0] arithmetic_unit_16_bit_1_result, logic_unit_16_bit_1_logic_unit_output, SetOut,
       shift_unit_16_bit_1_shift_unit_output;

  Shift_Unit_16_bit shift_unit_16_bit_1 (
    .Shift_input(A), .Shift_Amount(B[3:0]), .Shift_unit_output(shift_unit_16_bit_1_shift_unit_output),
    .Shift_Mode(ALUOp[1:0]));
  Arithmetic_Unit_16_bit arithmetic_unit_16_bit_1 (
    .A(A), .B(B), .Result(arithmetic_unit_16_bit_1_result), .Overflow(Overflow), .Select(ALUOp[0]));
  Conditional_Set_Unit conditional_set_unit_1 (.A(A), .B(B), .Conditional_Set_sel(ALUOp[0]), .Conditional_sett(SetOut));
  Logic_Unit_16_bit logic_unit_16_bit_1 (
    .A(A), .B(B), .Logic_unit_output(logic_unit_16_bit_1_logic_unit_output), .Logic_unit_select(ALUOp[1:0]));
  Multiplexer #(.select(2), .width(16), .enable("false")) multiplexer_1 (
    .in0(shift_unit_16_bit_1_shift_unit_output), .in1(SetOut), .in2(arithmetic_unit_16_bit_1_result),
    .in3(logic_unit_16_bit_1_logic_unit_output), .out(ALU_Result), .sel(ALUOp[3:2]));
  nor nor_1 (ALU_zero, ALU_Result[15], ALU_Result[14], ALU_Result[13], ALU_Result[12], ALU_Result[11], ALU_Result[10], ALU_Result[9], ALU_Result[8], ALU_Result[7], ALU_Result[6], ALU_Result[5], ALU_Result[4], ALU_Result[3], ALU_Result[2], ALU_Result[1], ALU_Result[0]);

  // Other names for the same wires on the sheet: ALUSel[1:0] = ALUOp[3:2]; ALUZero = ALU_zero; ArithSEl = ALUOp[0];
  //   LogicSel[1:0] = ALUOp[1:0]; SetSel = ALUOp[0]; ShiftSel[1:0] = ALUOp[1:0]

  // Notes on the sheet:
  //   ALU Sel
  //   ALUSel= ALUOp[3:2]
  //   ShiftSel= ALUOp[1:0]
  //   SetSel= ALUOp[0]
  //   ArithSel= ALUOp[0]
  //   LogicSel= ALUOp[1:0]
  //   Flags
endmodule
