// Logisim project 16-bit ALU Test Revised.circ as structural Verilog: 1 circuit, main circuit main
module main (
  input  [15:0] in_1,
  input  [15:0] in_2,
  input  [3:0] in_3,
  output [15:0] out_4,
  output out_5,
  output out_6
);

  ALU_16_bit alu_16_bit_1 (.A(in_1), .B(in_2), .ALU_Result(out_4), .Overflow(out_5), .ALU_zero(out_6), .ALUOp(in_3));

  // Notes on the sheet:
  //   ALU Control:
  //   Unit
  //   Arith
  //   Logic
  //   ALUSel
  //   0 0
  //   Shift
  //   0 0
  //   0 1
  //   Set
  //   0 1
  //   1 0
  //   1 0
  //   1 1
  //   1 1
  //   1 1
  //   1 1
  //   32-bit ALU Test
  //   ALUFunc
  //   0 1
  //   1 0
  //   0 0
  //   0 1
  //   0 0
  //   0 1
  //   0 0
  //   0 1
  //   1 0
  //   1 1
  //   Function
  //   SLL
  //   SRL
  //   SEQ
  //   SLT
  //   ADD
  //   SUB
  //   AND
  //   OR
  //   XOR
  //   NOR
  //   Test Results:
  //   Arithmetic Unit: OK
  //   Logic Unit:  OK
  //   Shift Unit: OK 
  //   SET/SEQ: OK
  //   ALU
  //   Shift = 00
  //   Conditional SET= 01
  //   Arith = 10
  //   Logic = 11
  //   Shift Operations
  //   None = 00
  //   SLL = 01
  //   SRL = 10
  //   SRA= 11
  //   DataA = Shift amount
  //   DataB = Input to shift
  //   Select Inputs:
  //   ADD = 0
  //   SUB = 1
  //   Arithmetic Operations
  //   Logic Operations
  //   AND = 00
  //   OR = 01
  //   NOR = 10
  //   XOR = 11
endmodule
