// Logisim project 16-bit Instruction Splitter.circ as structural Verilog: 1 circuit, main circuit Instruction Splitter 16-bit
module Instruction_Splitter_16_bit (
  input  [15:0] Instruction,
  output [4:0] Opcodee,
  output [2:0] a,
  output [2:0] b,
  output [2:0] d,
  output [1:0] Func,
  output [4:0] Imm5,
  output [7:0] Imm8,
  output [10:0] Im11
);


  assign a = Instruction[10:8];
  assign b = Instruction[7:5];
  assign d = Instruction[4:2];
  assign Func = Instruction[1:0];
  assign Im11 = Instruction[10:0];
  assign Imm5 = Instruction[4:0];
  assign Imm8 = Instruction[7:0];
  assign Opcodee = Instruction[15:11];
endmodule
