// Logisim project 16-bit Single-Cycle Processor Module.circ as structural Verilog: 1 circuit, main circuit 16-bit Single Cycle Processor
module _16_bit_Single_Cycle_Processor (
  input  Clock,
  input  Data_Memory_clr,
  input  PC_clr,
  input  RegFile_clr,
  output [15:0] Reg_out_0,
  output [15:0] Reg_out_1,
  output [15:0] Reg_out_2,
  output [15:0] Reg_out_3,
  output [15:0] Reg_out_4,
  output [15:0] Reg_out_5,
  output [15:0] Reg_out_6,
  output [15:0] Reg_out_7,
  output [15:0] Next_PC_Value,
  output [15:0] out_14
);

  wire BEQZ, BGTZ, BLTZ, ExtOp, Jump_Sel, MemRd, MemWr, RegWr, WBdata, Zero;
  wire [1:0] Ad__WBSel, ALUSrc, Func, ImmSel, PCSrc, RegDst;
  wire [2:0] instruction_splitter_16_bit_1_a, instruction_splitter_16_bit_1_b,
       instruction_splitter_16_bit_1_d, reg_mux_1_rw;
  wire [3:0] ALUOp;
  wire [4:0] Op;
  wire [7:0] Imm8;
  wire [10:0] Imm11;
  wire [15:0] additional_wb_mux_1_to_wbdata, alu_16_bit_1_alu_result, alusrc_mux_1_alu_bin,
       alusrc_mux_2_alu_bin, Branch_Target, data_memory_16_bit_1_data_memory_output, Imm16,
       instruction_memory_16_bit_1_instruction_out, Jump_Target, Next_PC, Ra,
       register_file_8x16_bit_1_read_data_2, SSET_out, wb_mux_1_bus_w;

  Program_Counter program_counter_1 (.PC_in(Next_PC_Value), .PC_out(out_14), .Clk(Clock), .PC_Clr(PC_clr));
  PC_Mux pc_mux_1 (
    .Next_PC_Address(Next_PC), .Jump_Target(Jump_Target), .Branch_Target_Address(Branch_Target),
    .PC_Input(Next_PC_Value), .PCSrc(PCSrc));
  Jump_Calculator jump_calculator_1 (
    .PC(out_14), .Jump_Target(Jump_Target), .Imm16(Imm16), .Ra(Ra), .Jump_Sel(Jump_Sel));
  PC_Incrementer pc_incrementer_1 (.in_1(out_14), .out_2(Next_PC));
  PC_Control pc_control_1 (.Opcode(Op), .PCSrc(PCSrc), .BGEZ_flag(BGTZ), .BEQZ_flag(BEQZ), .BLTZ_flag(BLTZ));
  Branch_Caalculator branch_caalculator_1 (
    .Next_PC_Address(Next_PC), ._16_bit_Extended_Immediate(Imm16), .Branch_Target_Address(Branch_Target));
  Instruction_Memory_16_bit instruction_memory_16_bit_1 (
    .Instruction_Address(out_14), .Instruction_out(instruction_memory_16_bit_1_instruction_out));
  Extender extender_1 (.ImmExt16(Imm16), .ExtOP(ExtOp), .Imm11(Imm11), .ImmSel(ImmSel));
  Instruction_Splitter_16_bit instruction_splitter_16_bit_1 (
    .Instruction(instruction_memory_16_bit_1_instruction_out), .Opcodee(Op),
    .a(instruction_splitter_16_bit_1_a), .b(instruction_splitter_16_bit_1_b),
    .d(instruction_splitter_16_bit_1_d), .Func(Func), .Imm8(Imm8), .Im11(Imm11));  // open: Imm5
  Reg_Mux reg_mux_1 (
    .Rt(3'b111), .Rw(reg_mux_1_rw), .Rd(instruction_splitter_16_bit_1_d), .RegDst(RegDst),
    .Ra(instruction_splitter_16_bit_1_a));
  Main_Control main_control_1 (
    .Op(Op), .RegDst(RegDst), .RegWr(RegWr), .ExtOp(ExtOp), .ALUSrc(ALUSrc), .MemRd(MemRd), .MemWr(MemWr),
    .WBData(WBdata), .AdditionalWBSel(Ad__WBSel), .out_10(ImmSel), .out_11(Jump_Sel));
  Branch_Flags branch_flags_1 (.A(Ra), .A_B(BGTZ), .A___B(BEQZ), .A___B_2(BLTZ));
  Register_File_8x16_bit register_file_8x16_bit_1 (
    .Write_Data(wb_mux_1_bus_w), .Read_Data_1(Ra), .Read_Data_2(register_file_8x16_bit_1_read_data_2),
    .WriteRegister(reg_mux_1_rw), .RegWrite(RegWr), .Clock(Clock),
    .Read_Register_1(instruction_splitter_16_bit_1_a), .Read_Register_2(instruction_splitter_16_bit_1_b),
    .Reg_out_0(Reg_out_0), .Reg_out_1(Reg_out_1), .Reg_out_2(Reg_out_2), .Reg_out_3(Reg_out_3),
    .Reg_out_4(Reg_out_4), .Reg_out_5(Reg_out_5), .Reg_out_6(Reg_out_6), .Reg_out_7(Reg_out_7),
    .clr(RegFile_clr));
  ALU_Control alu_control_1 (.func(Func), .Op(Op), .ALUOp(ALUOp));
  SSET_Unit sset_unit_1 (.Imm8(Imm8), .SSET_out(SSET_out), .A(Ra));
  ALUsrc_Mux alusrc_mux_1 (
    .Ext(Ra), .BusB(register_file_8x16_bit_1_read_data_2), .ALU_Bin(alusrc_mux_1_alu_bin), .ALUSrc(ALUSrc[1]));
  ALUsrc_Mux alusrc_mux_2 (
    .Ext(register_file_8x16_bit_1_read_data_2), .BusB(Imm16), .ALU_Bin(alusrc_mux_2_alu_bin),
    .ALUSrc(ALUSrc[0]));
  ALU_16_bit alu_16_bit_1 (
    .A(alusrc_mux_1_alu_bin), .B(alusrc_mux_2_alu_bin), .ALU_Result(alu_16_bit_1_alu_result),
    .ALU_zero(Zero), .ALUOp(ALUOp));  // open: Overflow
  Additional_WB_mux additional_wb_mux_1 (
    .Imm16(Imm16), .SSETImm16(SSET_out), .to_WBData(additional_wb_mux_1_to_wbdata), .ALUSrc(WBdata),
    .ImmSel(Ad__WBSel), .ALUOut(alu_16_bit_1_alu_result), .to_R7(Next_PC));
  Data_Memory_16_bit data_memory_16_bit_1 (
    .Address(alu_16_bit_1_alu_result), .Data_in(Ra),
    .Data_Memory_Output(data_memory_16_bit_1_data_memory_output), .Store(MemWr), .Clock(Clock), .Load(MemRd),
    .Clr(Data_Memory_clr));
  WB_Mux wb_mux_1 (
    .Ad_WB_MUX_Data(additional_wb_mux_1_to_wbdata), .Data_Mem_out(data_memory_16_bit_1_data_memory_output),
    .Bus_W(wb_mux_1_bus_w), .WB_Data(WBdata));

  // Other names for the same wires on the sheet: clk = Clock; PC[15:0] = out_14; R0[15:0] = Reg_out_0;
  //   R1[15:0] = Reg_out_1; R2[15:0] = Reg_out_2; R3[15:0] = Reg_out_3; R4[15:0] = Reg_out_4; R5[15:0] = Reg_out_5;
  //   R6[15:0] = Reg_out_6; R7[15:0] = Reg_out_7

  // Notes on the sheet:
  //   Jump Dest. Calculator
  //   __________________
  //   Branch Target Calc
  //   _________________
  //   Control 
  //   ___________________________________________________________
  //   Extender
  //   Instruction Specific
  //   ______________
  //   Clock
  //   _________
  //   16-bit Single Cycle Processor
  //   ______________________________________________-______________________
  //   Enable
  //   _________
  //   Register File Registers R0 - R7
  //   _______________________________________________________
endmodule
