// Logisim project 16-bit Single-Cycle Processor Test.circ as structural Verilog: 1 circuit, main circuit main
module main (
  output [15:0] Program_Counter,
  output [15:0] out_2,
  output [15:0] out_3,
  output [15:0] Next_Program_Counter,
  output [15:0] out_5,
  output [15:0] out_6,
  output [15:0] out_7,
  output [15:0] out_8,
  output [15:0] out_9,
  output [15:0] out_10
);

  wire button_1_out, button_2_out, button_3_out, clock_1_out;
  wire [3:0] n16_bit_to_4_bit_1__0, n16_bit_to_4_bit_1__1, n16_bit_to_4_bit_1__2, n16_bit_to_4_bit_1__3,
       n16_bit_to_4_bit_2__0, n16_bit_to_4_bit_2__1, n16_bit_to_4_bit_2__2, n16_bit_to_4_bit_2__3,
       n16_bit_to_4_bit_3__0, n16_bit_to_4_bit_3__1, n16_bit_to_4_bit_3__2, n16_bit_to_4_bit_3__3,
       n16_bit_to_4_bit_4__0, n16_bit_to_4_bit_4__1, n16_bit_to_4_bit_4__2, n16_bit_to_4_bit_4__3,
       n16_bit_to_4_bit_5__0, n16_bit_to_4_bit_5__1, n16_bit_to_4_bit_5__2, n16_bit_to_4_bit_5__3,
       n16_bit_to_4_bit_6__0, n16_bit_to_4_bit_6__1, n16_bit_to_4_bit_6__2, n16_bit_to_4_bit_6__3;

  Clock clock_1 (.out(clock_1_out));
  Button button_1 (.out(button_1_out));
  Hex_Digit_Display hex_digit_display_1 (.value(n16_bit_to_4_bit_1__3));  // open: dp
  Hex_Digit_Display hex_digit_display_2 (.value(n16_bit_to_4_bit_2__3));  // open: dp
  _16_bit_Single_Cycle_Processor u_16_bit_single_cycle_processor_1 (
    .Reg_out_0(out_2), .Reg_out_4(out_7), .Reg_out_1(out_3), .Reg_out_5(out_8), .Reg_out_2(out_5),
    .Reg_out_6(out_9), .Reg_out_3(out_6), .Reg_out_7(out_10), .Data_Memory_clr(button_3_out),
    .PC_clr(button_1_out), .RegFile_clr(button_2_out), .Clock(clock_1_out), .out_14(Program_Counter),
    .Next_PC_Value(Next_Program_Counter));
  Button button_2 (.out(button_2_out));
  Button button_3 (.out(button_3_out));
  Hex_Digit_Display hex_digit_display_3 (.value(n16_bit_to_4_bit_1__1));  // open: dp
  Hex_Digit_Display hex_digit_display_4 (.value(n16_bit_to_4_bit_1__2));  // open: dp
  Hex_Digit_Display hex_digit_display_5 (.value(n16_bit_to_4_bit_2__1));  // open: dp
  Hex_Digit_Display hex_digit_display_6 (.value(n16_bit_to_4_bit_2__2));  // open: dp
  Hex_Digit_Display hex_digit_display_7 (.value(n16_bit_to_4_bit_1__0));  // open: dp
  _16_bit_to_4_bit u_16_bit_to_4_bit_1 (
    .n6_bit_in(Program_Counter), ._0(n16_bit_to_4_bit_1__0), ._1(n16_bit_to_4_bit_1__1),
    ._2(n16_bit_to_4_bit_1__2), ._3(n16_bit_to_4_bit_1__3));
  Hex_Digit_Display hex_digit_display_8 (.value(n16_bit_to_4_bit_2__0));  // open: dp
  _16_bit_to_4_bit u_16_bit_to_4_bit_2 (
    .n6_bit_in(Next_Program_Counter), ._0(n16_bit_to_4_bit_2__0), ._1(n16_bit_to_4_bit_2__1),
    ._2(n16_bit_to_4_bit_2__2), ._3(n16_bit_to_4_bit_2__3));
  Hex_Digit_Display hex_digit_display_9 (.value(n16_bit_to_4_bit_3__2));  // open: dp
  Hex_Digit_Display hex_digit_display_10 (.value(n16_bit_to_4_bit_3__3));  // open: dp
  Hex_Digit_Display hex_digit_display_11 (.value(n16_bit_to_4_bit_4__3));  // open: dp
  Hex_Digit_Display hex_digit_display_12 (.value(n16_bit_to_4_bit_4__2));  // open: dp
  Hex_Digit_Display hex_digit_display_13 (.value(n16_bit_to_4_bit_5__3));  // open: dp
  Hex_Digit_Display hex_digit_display_14 (.value(n16_bit_to_4_bit_5__2));  // open: dp
  Hex_Digit_Display hex_digit_display_15 (.value(n16_bit_to_4_bit_6__2));  // open: dp
  Hex_Digit_Display hex_digit_display_16 (.value(n16_bit_to_4_bit_6__3));  // open: dp
  Hex_Digit_Display hex_digit_display_17 (.value(n16_bit_to_4_bit_3__0));  // open: dp
  Hex_Digit_Display hex_digit_display_18 (.value(n16_bit_to_4_bit_3__1));  // open: dp
  _16_bit_to_4_bit u_16_bit_to_4_bit_3 (
    .n6_bit_in(out_2), ._0(n16_bit_to_4_bit_3__0), ._1(n16_bit_to_4_bit_3__1), ._2(n16_bit_to_4_bit_3__2),
    ._3(n16_bit_to_4_bit_3__3));
  Hex_Digit_Display hex_digit_display_19 (.value(n16_bit_to_4_bit_4__0));  // open: dp
  Hex_Digit_Display hex_digit_display_20 (.value(n16_bit_to_4_bit_4__1));  // open: dp
  _16_bit_to_4_bit u_16_bit_to_4_bit_4 (
    .n6_bit_in(out_3), ._0(n16_bit_to_4_bit_4__0), ._1(n16_bit_to_4_bit_4__1), ._2(n16_bit_to_4_bit_4__2),
    ._3(n16_bit_to_4_bit_4__3));
  Hex_Digit_Display hex_digit_display_21 (.value(n16_bit_to_4_bit_5__1));  // open: dp
  Hex_Digit_Display hex_digit_display_22 (.value(n16_bit_to_4_bit_5__0));  // open: dp
  _16_bit_to_4_bit u_16_bit_to_4_bit_5 (
    .n6_bit_in(out_5), ._0(n16_bit_to_4_bit_5__0), ._1(n16_bit_to_4_bit_5__1), ._2(n16_bit_to_4_bit_5__2),
    ._3(n16_bit_to_4_bit_5__3));
  Hex_Digit_Display hex_digit_display_23 (.value(n16_bit_to_4_bit_6__0));  // open: dp
  Hex_Digit_Display hex_digit_display_24 (.value(n16_bit_to_4_bit_6__1));  // open: dp
  _16_bit_to_4_bit u_16_bit_to_4_bit_6 (
    .n6_bit_in(out_6), ._0(n16_bit_to_4_bit_6__0), ._1(n16_bit_to_4_bit_6__1), ._2(n16_bit_to_4_bit_6__2),
    ._3(n16_bit_to_4_bit_6__3));

  // Other names for the same wires on the sheet: Next_PC[15:0] = Next_Program_Counter; PC[15:0] = Program_Counter;
  //   R0[15:0] = out_2; R1[15:0] = out_3; R2[15:0] = out_5; R3[15:0] = out_6; R4[15:0] = out_7; R5[15:0] = out_8;
  //   R6[15:0] = out_9; R7[15:0] = out_10

  // Notes on the sheet:
  //   PC
  //   NEXT
  //   PC
  //   16-bit Single Cycle Processor Test
  //   Hex
  //   R0
  //   R1
  //   R2
  //   R3
  //   Binary
  //   Registers
endmodule
