// Logisim project 16-bit to hex.circ as structural Verilog: 1 circuit, main circuit 16-bit to 4 bit 
module _16_bit_to_4_bit (
  input  [15:0] n6_bit_in,
  output [3:0] _0,
  output [3:0] _1,
  output [3:0] _2,
  output [3:0] _3
);


  assign _0 = n6_bit_in[3:0];
  assign _1 = n6_bit_in[7:4];
  assign _2 = n6_bit_in[11:8];
  assign _3 = n6_bit_in[15:12];
endmodule
