// Logisim project 8x16-bit Register File.circ as structural Verilog: 1 circuit, main circuit Register File 8x16-bit
module Register_File_8x16_bit (
  input  [2:0] Read_Register_1,
  input  [2:0] WriteRegister,
  input  [15:0] Write_Data,
  input  [2:0] Read_Register_2,
  input  RegWrite,
  input  Clock,
  input  clr,
  output [15:0] Reg_out_0,
  output [15:0] Reg_out_1,
  output [15:0] Reg_out_2,
  output [15:0] Reg_out_3,
  output [15:0] Reg_out_4,
  output [15:0] Reg_out_5,
  output [15:0] Reg_out_6,
  output [15:0] Reg_out_7,
  output [15:0] Read_Data_1,
  output [15:0] Read_Data_2
);

  wire and_1_out, and_2_out, and_3_out, and_4_out, and_5_out, and_6_out, and_7_out, and_8_out,
       decoder_1_out0, decoder_1_out1, decoder_1_out2, decoder_1_out3, decoder_1_out4, decoder_1_out5,
       decoder_1_out6, decoder_1_out7;

  Decoder #(.select(3)) decoder_1 (
    .out0(decoder_1_out0), .out1(decoder_1_out1), .out2(decoder_1_out2), .out3(decoder_1_out3),
    .out4(decoder_1_out4), .out5(decoder_1_out5), .out6(decoder_1_out6), .out7(decoder_1_out7),
    .sel(WriteRegister), .en(1'b1));
  and and_1 (and_1_out, decoder_1_out0, RegWrite);
  and and_2 (and_2_out, decoder_1_out1, RegWrite);
  and and_3 (and_3_out, decoder_1_out2, RegWrite);
  and and_4 (and_4_out, decoder_1_out3, RegWrite);
  and and_5 (and_5_out, decoder_1_out4, RegWrite);
  and and_6 (and_6_out, decoder_1_out5, RegWrite);
  and and_7 (and_7_out, decoder_1_out6, RegWrite);
  and and_8 (and_8_out, decoder_1_out7, RegWrite);
  Register #(.width(16)) register_1 (.D(Write_Data), .en(and_1_out), .Q(Reg_out_0), .clk(Clock), .clr(clr));
  Register #(.width(16)) register_2 (.D(Write_Data), .en(and_2_out), .Q(Reg_out_1), .clk(Clock), .clr(clr));
  Register #(.width(16)) register_3 (.D(Write_Data), .en(and_3_out), .Q(Reg_out_2), .clk(Clock), .clr(clr));
  Register #(.width(16)) register_4 (.D(Write_Data), .en(and_4_out), .Q(Reg_out_3), .clk(Clock), .clr(clr));
  Register #(.width(16)) register_5 (.D(Write_Data), .en(and_5_out), .Q(Reg_out_4), .clk(Clock), .clr(clr));
  Register #(.width(16)) register_6 (.D(Write_Data), .en(and_6_out), .Q(Reg_out_5), .clk(Clock), .clr(clr));
  Register #(.width(16)) register_7 (.D(Write_Data), .en(and_7_out), .Q(Reg_out_6), .clk(Clock), .clr(clr));
  Register #(.width(16)) register_8 (.D(Write_Data), .en(and_8_out), .Q(Reg_out_7), .clk(Clock), .clr(clr));
  Multiplexer #(.select(3), .width(16)) multiplexer_1 (
    .in0(Reg_out_0), .in1(Reg_out_1), .in2(Reg_out_2), .in3(Reg_out_3), .in4(Reg_out_4), .in5(Reg_out_5),
    .in6(Reg_out_6), .in7(Reg_out_7), .out(Read_Data_1), .sel(Read_Register_1), .en(1'b1));
  Multiplexer #(.select(3), .width(16)) multiplexer_2 (
    .in0(Reg_out_0), .in1(Reg_out_1), .in2(Reg_out_2), .in3(Reg_out_3), .in4(Reg_out_4), .in5(Reg_out_5),
    .in6(Reg_out_6), .in7(Reg_out_7), .out(Read_Data_2), .sel(Read_Register_2), .en(1'b1));

  // Notes on the sheet:
  //   Write Bus
  //   R0
  //   R1
  //   R2
  //   R3
  //   R4
  //   R5
  //   R6
  //   R7
  //   Read Bus B
  //   Read Bus A
endmodule
