// Logisim project ALU src MUX.circ as structural Verilog: 1 circuit, main circuit ALUsrc Mux
module ALUsrc_Mux (
  input  [15:0] Ext,
  input  [15:0] BusB,
  input  ALUSrc,
  output [15:0] ALU_Bin
);

  Multiplexer #(.width(16)) multiplexer_1 (.in0(Ext), .in1(BusB), .out(ALU_Bin), .sel(ALUSrc), .en(1'b1));
endmodule
