// Logisim project Branch Target Calculator.circ as structural Verilog: 1 circuit, main circuit Branch Caalculator
module Branch_Caalculator (
  input  [15:0] Next_PC_Address,
  input  [15:0] _16_bit_Extended_Immediate,
  output [15:0] Branch_Target_Address
);

  Adder #(.width(16)) adder_1 (
    .a(Next_PC_Address), .b(_16_bit_Extended_Immediate), .out(Branch_Target_Address), .cin(1'b0));  // open: cout
endmodule
