// Logisim project Conditional Set Unit.circ as structural Verilog: 1 circuit, main circuit Conditional Set Unit
module Conditional_Set_Unit (
  input  [15:0] A,
  input  [15:0] B,
  input  Conditional_Set_sel,
  output [15:0] Conditional_sett
);

  wire comparator_1_eq, comparator_1_lt, multiplexer_1_out;

  Comparator #(.width(16)) comparator_1 (.a(A), .b(B), .eq(comparator_1_eq), .lt(comparator_1_lt));  // open: gt
  Multiplexer #(.enable("false")) multiplexer_1 (
    .in0(comparator_1_eq), .in1(comparator_1_lt), .out(multiplexer_1_out), .sel(Conditional_Set_sel));
  assign Conditional_sett = {{15{1'b0}}, multiplexer_1_out};  // Bit_Extender bit_extender_1
endmodule
