// Logisim project Instruction Memory.circ as structural Verilog: 1 circuit, main circuit Instruction Memory 16-bit
module Instruction_Memory_16_bit (
  input  [15:0] Instruction_Address,
  output [15:0] Instruction_out
);

  ROM #(.addrWidth(16), .dataWidth(16)) rom_1 (.addr(Instruction_Address), .data(Instruction_out), .sel(1'b1));
endmodule
