// Logisim project Jump Calculator.circ as structural Verilog: 1 circuit, main circuit Jump Calculator
module Jump_Calculator (
  input  [15:0] Ra,
  input  [15:0] Imm16,
  input  [15:0] PC,
  input  Jump_Sel,
  output [15:0] Jump_Target
);

  wire [15:0] multiplexer_1_out, multiplexer_2_out;

  Multiplexer #(.width(16), .enable("false")) multiplexer_1 (
    .in0(Ra), .in1(Imm16), .out(multiplexer_1_out), .sel(Jump_Sel));
  Multiplexer #(.width(16), .enable("false")) multiplexer_2 (
    .in0(Imm16), .in1(PC), .out(multiplexer_2_out), .sel(Jump_Sel));
  Adder #(.width(16)) adder_1 (.a(multiplexer_1_out), .b(multiplexer_2_out), .out(Jump_Target));  // open: cin, cout
endmodule
