// Logisim project Main Control.circ as structural Verilog: 1 circuit, main circuit Main Control
module Main_Control (
  input  [4:0] Op,
  output [1:0] RegDst,
  output ExtOp,
  output MemRd,
  output RegWr,
  output [1:0] ALUSrc,
  output MemWr,
  output WBData,
  output [1:0] AdditionalWBSel,
  output [1:0] out_10,
  output out_11
);

  wire _0, _1, _2, _3, _4, _5, _6, _7, _8, _9, _10, _11, _12, _13, _14, _15, _18, _19, _20, _21, _22, _23,
       _24, _25, _26, _27, _28, _29, _30, _31, Branch_Op_20___25, I_Type_Op_4__11, Shift;

  or or_1 (RegDst[0], _0, _1);
  Decoder #(.select(5), .enable("false")) decoder_1 (
    .out0(_0), .out1(_1), .out2(_2), .out3(_3), .out4(_4), .out5(_5), .out6(_6), .out7(_7), .out8(_8),
    .out9(_9), .out10(_10), .out11(_11), .out12(_12), .out13(_13), .out14(_14), .out15(_15), .out16(MemRd),
    .out17(MemWr), .out18(_18), .out19(_19), .out20(_20), .out21(_21), .out22(_22), .out23(_23), .out24(_24),
    .out25(_25), .out26(_26), .out27(_27), .out28(_28), .out29(_29), .out30(_30), .out31(_31), .sel(Op));
  or or_2 (RegDst[1], I_Type_Op_4__11, Shift, MemRd, MemWr, _28, _29);
  or or_3 (AdditionalWBSel[1], _31, _27, _29);
  or or_4 (I_Type_Op_4__11, _4, _5, _6, _7, _8, _9, _10, _11);
  or or_5 (AdditionalWBSel[0], _31, _28, _27);
  or or_6 (Shift, _12, _13);
  or or_7 (out_10[1], _30, _31);
  or or_8 (RegWr, RegDst[0], I_Type_Op_4__11, Shift, MemRd, _27, _29, _28, _31);
  or or_9 (out_10[0], Branch_Op_20___25, _26, _27, _28, _29);
  or or_10 (Branch_Op_20___25, _20, _21, _22, _23, _24, _25);
  or or_11 (ALUSrc[1], MemRd, MemWr, Shift, I_Type_Op_4__11);
  not not_1 (ExtOp, Shift);
  or or_12 (out_11, _30, _31);

  assign ALUSrc[0] = ALUSrc[1];
  assign WBData = MemRd;

  // Other names for the same wires on the sheet: ImmSel[1:0] = out_10; J = _30; JAL = _31; JALR = _27; JR = _26;
  //   Jump_Sel = out_11; _16 = MemRd; LW = MemRd; R_type_Op_0_1 = RegDst[0]; SET = _28; SSET = _29; _17 = MemWr;
  //   SW = MemWr

  // Notes on the sheet:
  //   Input: Opcode 5-bit
  //   Main Control
  //   ____________________
  //   Outputs:
endmodule
