// Logisim project PC Incrementer 16-biit.circ as structural Verilog: 1 circuit, main circuit PC Incrementer
module PC_Incrementer (
  input  [15:0] in_1,
  output [15:0] out_2
);

  Adder #(.width(15)) adder_1 (.a(15'h1), .b(in_1[15:1]), .out(out_2[15:1]));  // open: cin, cout

  assign out_2[0] = in_1[0];
endmodule
