// Logisim project PC Mux.circ as structural Verilog: 1 circuit, main circuit PC Mux
module PC_Mux (
  input  [15:0] Next_PC_Address,
  input  [15:0] Jump_Target,
  input  [15:0] Branch_Target_Address,
  input  [1:0] PCSrc,
  output [15:0] PC_Input
);

  Multiplexer #(.select(2), .width(16)) multiplexer_1 (
    .in0(Next_PC_Address), .in1(Branch_Target_Address), .in2(Jump_Target), .in3({16{1'b0}}), .out(PC_Input),
    .sel(PCSrc), .en(1'b1));
endmodule
