// Logisim project Program Counter 16-bit.circ as structural Verilog: 1 circuit, main circuit Program Counter
module Program_Counter (
  input  [15:0] PC_in,
  input  Clk,
  input  PC_Clr,
  output [15:0] PC_out
);

  Register #(.width(16)) register_1 (.D(PC_in), .en(1'b1), .Q(PC_out), .clk(Clk), .clr(PC_Clr));
endmodule
