// Logisim project Write Back Mux.circ as structural Verilog: 1 circuit, main circuit WB Mux
module WB_Mux (
  input  [15:0] Ad_WB_MUX_Data,
  input  [15:0] Data_Mem_out,
  input  WB_Data,
  output [15:0] Bus_W
);

  Multiplexer #(.width(16), .enable("false")) multiplexer_1 (
    .in0(Ad_WB_MUX_Data), .in1(Data_Mem_out), .out(Bus_W), .sel(WB_Data));
endmodule
